// Logisim project tinyproc2.circ as structural Verilog: 2 circuits, main circuit main
module main (
  input  Clock,
  output [1:0] SR1,
  output [1:0] SR2,
  output [1:0] out_4,
  output [7:0] out_5,
  output [7:0] out_6,
  output [7:0] DR_S1_S2_Op,
  output [1:0] Operation,
  output [7:0] out_9
);

  wire and_1_out, and_2_out, and_3_out, and_4_out, decoder_1_out0, decoder_1_out1, decoder_1_out2,
       decoder_1_out3, not_1_out;
  wire [7:0] adder_1_out, counter_1_q, immediate_1_out_2, multiplier_1_out, ram_1_data, register_2_q,
       register_3_q, register_4_q, register_5_q, subtractor_1_out;

  Decoder #(.select(2), .enable("false")) decoder_1 (
    .out0(decoder_1_out0), .out1(decoder_1_out1), .out2(decoder_1_out2), .out3(decoder_1_out3),
    .sel(DR_S1_S2_Op[7:6]));
  Counter counter_1 (.Q(counter_1_q), .clk(Clock));  // open: load, D, count, carry, clr
  not not_1 (not_1_out, Clock);
  and and_1 (and_1_out, not_1_out, decoder_1_out0);
  and and_2 (and_2_out, not_1_out, decoder_1_out1);
  and and_3 (and_3_out, not_1_out, decoder_1_out2);
  and and_4 (and_4_out, not_1_out, decoder_1_out3);
  RAM ram_1 (.addr(counter_1_q), .data(ram_1_data));  // open: sel, clk, ld, clr
  Register register_1 (.D(ram_1_data), .Q(DR_S1_S2_Op), .clk(Clock));  // open: en, clr
  Register register_2 (.D(out_9), .Q(register_2_q), .clk(and_1_out));  // open: en, clr
  Register register_3 (.D(out_9), .Q(register_3_q), .clk(and_2_out));  // open: en, clr
  Multiplexer #(.select(2), .width(8), .enable("false")) multiplexer_1 (
    .in0(register_2_q), .in1(register_3_q), .in2(register_4_q), .in3(register_5_q), .out(out_5),
    .sel(DR_S1_S2_Op[5:4]));
  Adder adder_1 (.a(out_5), .b(out_6), .out(adder_1_out));  // open: cin, cout
  Register register_4 (.D(out_9), .Q(register_4_q), .clk(and_3_out));  // open: en, clr
  Subtractor subtractor_1 (.a(out_5), .b(out_6), .out(subtractor_1_out));  // open: bin, bout
  Multiplexer #(.select(2), .width(8), .enable("false")) multiplexer_2 (
    .in0(adder_1_out), .in1(subtractor_1_out), .in2(multiplier_1_out), .in3(immediate_1_out_2), .out(out_9),
    .sel(DR_S1_S2_Op[1:0]));
  Register register_5 (.D(out_9), .Q(register_5_q), .clk(and_4_out));  // open: en, clr
  Multiplexer #(.select(2), .width(8), .enable("false")) multiplexer_3 (
    .in0(register_2_q), .in1(register_3_q), .in2(register_4_q), .in3(register_5_q), .out(out_6),
    .sel(DR_S1_S2_Op[3:2]));
  Multiplier multiplier_1 (.a(out_5), .b(out_6), .out(multiplier_1_out));  // open: cin, cout
  immediate immediate_1 (.in_1(DR_S1_S2_Op), .out_2(immediate_1_out_2));

  assign Operation = DR_S1_S2_Op[1:0];
  assign out_4 = DR_S1_S2_Op[7:6];
  assign SR1 = DR_S1_S2_Op[5:4];
  assign SR2 = DR_S1_S2_Op[3:2];

  // Notes on the sheet:
  //   Program
  //   Counter
  //   Instructions:
  //   Format: DR SR1 SR2 Op
  //   Opcodes: 00 Add
  //   Opcodes: 01 Sub
  //   Opcodes: 10 Mul
  //   Opcodes: 11 load imm.
  //   Save Registers
  //   Destination Reg DR
  //   Main Memory
  //   Inst. Reg
  //   A,00
  //   Current Instruction
  //   REGISTERS
  //   B,01
  //   For load immediate, the middle 4 bits are routed to the dest. register
  //   C,10
  //   Arithmetic/Logic Unit (ALU)
  //   D,11
endmodule

module immediate (
  input  [7:0] in_1,
  output [7:0] out_2
);


  assign out_2 = {{5{in_1[5]}}, in_1[4:2]};
endmodule
