// Logisim project adder.circ as structural Verilog: 5 circuits, main circuit adder
module adder (
  input  in_1,
  input  in_2,
  input  in_3,
  input  in_4,
  input  in_5,
  input  in_6,
  input  in_7,
  input  in_8,
  output out_9,
  output out_10,
  output out_11,
  output out_12
);

  wire fadd_2_out_4, fadd_3_out_4, hadd_1_c;

  fadd fadd_1 (.A(in_1), .B(in_5), .Ci(fadd_2_out_4), .out_5(out_9));  // open: out_4
  fadd fadd_2 (.A(in_2), .B(in_6), .Ci(fadd_3_out_4), .out_4(fadd_2_out_4), .out_5(out_10));
  fadd fadd_3 (.A(in_3), .B(in_3), .Ci(hadd_1_c), .out_4(fadd_3_out_4), .out_5(out_11));
  hadd hadd_1 (.A(in_8), .B(in_4), .C(hadd_1_c), .S(out_12));

  assign in_7 = in_3;
endmodule

module hadd (
  input  A,
  input  B,
  output C,
  output S
);

  and and_1 (C, B, A);
  xor xor_1 (S, A, B);
endmodule

module fadd (
  input  A,
  input  B,
  input  Ci,
  output out_4,
  output out_5
);

  wire and_1_out, and_2_out, and_3_out, xor_1_out;

  and and_1 (and_1_out, A, B);
  and and_2 (and_2_out, A, Ci);
  or or_1 (out_4, and_1_out, and_2_out, and_3_out);
  and and_3 (and_3_out, B, Ci);
  xor xor_1 (xor_1_out, B, A);
  xor xor_2 (out_5, xor_1_out, Ci);
endmodule

module add_sub (
  input  in_1,
  input  in_2,
  input  in_3,
  input  in_4,
  input  in_5,
  input  in_6,
  input  in_7,
  input  in_8,
  input  in_9,
  output out_10,
  output out_11,
  output out_12,
  output out_13
);

  wire fadd_2_out_4, fadd_3_out_4, fadd_4_out_4, xor_1_out, xor_2_out, xor_3_out, xor_4_out;

  fadd fadd_1 (.A(in_1), .B(xor_1_out), .Ci(fadd_2_out_4), .out_5(out_10));  // open: out_4
  xor xor_1 (xor_1_out, in_5, in_9);
  fadd fadd_2 (.A(in_2), .B(xor_2_out), .Ci(fadd_3_out_4), .out_4(fadd_2_out_4), .out_5(out_11));
  xor xor_2 (xor_2_out, in_6, in_9);
  xor xor_3 (xor_3_out, in_7, in_9);
  fadd fadd_3 (.A(in_3), .B(xor_3_out), .Ci(fadd_4_out_4), .out_4(fadd_3_out_4), .out_5(out_12));
  fadd fadd_4 (.A(in_4), .B(xor_4_out), .Ci(in_9), .out_4(fadd_4_out_4), .out_5(out_13));
  xor xor_4 (xor_4_out, in_8, in_9);
endmodule

module _157minterms (
  input  A,
  input  B,
  input  C,
  output O
);

  wire and_1_out, and_2_out, and_3_out, not_1_out, not_2_out, or_1_out;

  not not_1 (not_1_out, A);
  or or_1 (or_1_out, A, not_1_out);
  not not_2 (not_2_out, B);
  and and_1 (and_1_out, or_1_out, not_2_out);
  and and_2 (and_2_out, C, and_1_out);
  and and_3 (and_3_out, A, C, B);
  or or_2 (O, and_3_out, and_2_out);
endmodule
