// Logisim project part1.circ as structural Verilog: 1 circuit, main circuit main
module main (
  input  A,
  input  B,
  input  C,
  output out_4
);

  wire and_1_out, not_1_out, not_2_out, or_1_out;

  and and_1 (and_1_out, A, not_1_out);
  not not_1 (not_1_out, C);
  not not_2 (not_2_out, A);
  or or_1 (or_1_out, not_2_out, and_1_out, and_1_out);
  and and_2 (out_4, or_1_out, B);
endmodule
