// Logisim project part2.circ as structural Verilog: 1 circuit, main circuit main
module main (
  input  A,
  input  B,
  input  C,
  input  A_2,
  input  B_2,
  input  C_2,
  output out_7,
  output out_8
);

  wire and_1_out, and_2_out, xor_1_out;

  and and_1 (and_1_out, A, B);
  and and_2 (and_2_out, and_1_out, C);
  xor xor_1 (xor_1_out, and_1_out, and_2_out);
  or or_1 (out_7, xor_1_out, and_2_out, B);

  assign out_8 = B_2;

  // Notes on the sheet:
  //   Simplified
endmodule
