// Logisim project part3.circ as structural Verilog: 1 circuit, main circuit main
module main (
  input  A,
  input  C,
  input  S,
  input  R,
  input  A_2,
  input  C_2,
  input  S_2,
  input  R_2,
  output out_9,
  output out_10
);

  wire and_1_out, not_1_out, not_2_out, not_3_out, or_1_out, or_2_out, or_3_out;

  not not_1 (not_1_out, R);
  not not_2 (not_2_out, C);
  and and_1 (and_1_out, C, not_1_out);
  or or_1 (or_1_out, A_2, A_2, R_2, C_2);
  or or_2 (or_2_out, C_2, A_2, S_2);
  or or_3 (or_3_out, not_2_out, and_1_out);
  not not_3 (not_3_out, or_3_out);
  and and_2 (out_10, or_1_out, or_1_out, or_2_out);
  and and_3 (out_9, A, S, not_3_out);

  // Notes on the sheet:
  //   Simplified
endmodule
