// Logisim project lab1.circ as structural Verilog: 7 circuits, main circuit mux
module mux (
  input  in_1,
  input  in_2,
  input  in_3,
  output out_4
);

  wire and_1_out, and_2_out;

  and and_1 (and_1_out, in_1, ~in_3);  // AND_Gate
  and and_2 (and_2_out, in_2, in_3);
  or or_1 (out_4, and_1_out, and_2_out);
endmodule

module _2i4o_d (
  input  in_1,
  input  in_2,
  output out_3,
  output out_4,
  output out_5,
  output out_6
);

  and and_1 (out_3, ~in_1, ~in_2);  // AND_Gate
  and and_2 (out_4, ~in_1, in_2);  // AND_Gate
  and and_3 (out_5, in_1, ~in_2);  // AND_Gate
  and and_4 (out_6, in_1, in_2);
endmodule

module _2mux (
  input  in_1,
  input  in_2,
  input  in_3,
  input  in_4,
  input  in_5,
  input  in_6,
  output out_7
);

  wire mux_1_out_4, mux_2_out_4, not_1_out;

  not not_1 (not_1_out, in_5);
  mux mux_1 (.in_3(not_1_out), .out_4(mux_1_out_4), .in_1(in_1), .in_2(in_2));
  mux mux_2 (.in_3(in_5), .out_4(mux_2_out_4), .in_1(in_3), .in_2(in_4));
  mux mux_3 (.in_3(in_6), .out_4(out_7), .in_1(mux_1_out_4), .in_2(mux_2_out_4));
endmodule

module rslatch (
  input  in_1,
  input  in_2,
  output out_3,
  output out_4
);

  nor nor_1 (out_3, in_1, out_4);
  nor nor_2 (out_4, out_3, in_2);
endmodule

module dlatch (
  input  in_1,
  input  in_2,
  output out_3,
  output out_4
);

  wire and_1_out, and_2_out;

  and and_1 (and_1_out, in_1, ~in_2);  // AND_Gate
  and and_2 (and_2_out, in_1, in_2);
  rslatch rslatch_1 (.in_1(and_1_out), .in_2(and_2_out), .out_3(out_3), .out_4(out_4));
endmodule

module flipflop (
  input  in_1,
  input  in_2,
  output out_3,
  output out_4
);

  wire dlatch_1_out_3, not_1_out;

  not not_1 (not_1_out, in_1);
  dlatch dlatch_1 (.in_1(in_1), .in_2(in_2), .out_3(dlatch_1_out_3));  // open: out_4
  dlatch dlatch_2 (.in_1(not_1_out), .in_2(dlatch_1_out_3), .out_3(out_3), .out_4(out_4));
endmodule

module _4bitreg (
  input  in_1,
  input  in_2,
  input  in_3,
  input  in_4,
  input  in_5,
  output out_6,
  output out_7,
  output out_8,
  output out_9
);

  flipflop flipflop_1 (.in_1(in_5), .in_2(in_1), .out_3(out_6));  // open: out_4
  flipflop flipflop_2 (.in_1(in_5), .in_2(in_3), .out_3(out_8));  // open: out_4
  flipflop flipflop_3 (.in_1(in_5), .in_2(in_2), .out_3(out_7));  // open: out_4
  flipflop flipflop_4 (.in_1(in_5), .in_2(in_4), .out_3(out_9));  // open: out_4
endmodule
